# Fritzing sketch Major Project - CircuitHardwareDiagram (saved by Fritzing 0.9.3b)
breadboards: 1

parts:
  Raspberry_Pi_1 = Raspberry Pi 3 [part_number=RPI-3-V1.2]
  Part1 = Arduino Uno (Rev3)
  LED1 = smd LED [color="Infrared (850nm)" package="1206 [SMD]"]
  LED2 = smd LED [color="Green (555nm)" package="1206 [SMD]"]
  Part2 = Bluetooth HC-05 Macho

nets:
  N1: Raspberry_Pi_1.GPIO2, Part1.D6_PWM
  N2: Raspberry_Pi_1.GIPO17, Part1.D8
  GND: Raspberry_Pi_1.GND, Part1.GND, LED1.cathode, LED2.cathode, Part2.GND
  N3: Part1.D13/SCK, LED2.anode
  N4: Part1.D0/RX, Part2.RXD
  N5: Part1.D1/TX, Part2.TXD
  N6: Part1.D3_PWM, LED1.anode
  5V: Part1.5V, Part2.VCC
