# Fritzing sketch Major Project - IRHardware (saved by Fritzing 0.9.3b)

parts:
  Part1 = Arduino Uno (Rev3)
  IR1 = TSOP312.., 314.. [package=THT]
  LED1 = LED - 5mm [color="Red (633nm)" package="5 mm [THT]"]

nets:
  N1: Part1.D13/SCK, LED1.cathode
  GND: Part1.GND, IR1.GND, LED1.anode
  N2: Part1.D7, IR1.Data
  N3: Part1.5V, IR1.Vs
